// Logisim project Ctl_Conditional.circ as structural Verilog: 1 circuit, main circuit Conditional
module Conditional (
  input  [15:0] Instruction,
  input  Z,
  input  C,
  input  N,
  input  V,
  input  Enable,
  output [10:0] Offset,
  output Verified
);

  wire and_1_out, and_2_out, and_3_out, multiplexer_1_out, not_1_out, not_2_out, not_3_out, not_4_out,
       not_5_out, or_1_out, xor_1_out;

  not not_1 (not_1_out, Z);
  not not_2 (not_2_out, C);
  not not_3 (not_3_out, N);
  not not_4 (not_4_out, V);
  and and_1 (and_1_out, C, not_1_out);
  or or_1 (or_1_out, Z, not_2_out);
  xor xor_1 (xor_1_out, V, N);
  not not_5 (not_5_out, xor_1_out);
  and and_2 (and_2_out, not_1_out, not_5_out);
  and and_3 (and_3_out, Z, xor_1_out);
  Multiplexer #(.select(4)) multiplexer_1 (
    .in0(Z), .in1(not_1_out), .in2(C), .in3(not_2_out), .in4(N), .in5(not_3_out), .in6(V), .in7(not_4_out),
    .in8(and_1_out), .in9(or_1_out), .in10(not_5_out), .in11(xor_1_out), .in12(and_2_out), .in13(and_3_out),
    .in14(1'b1), .out(multiplexer_1_out), .sel(Instruction[3:0]));  // open: in15
  and and_4 (Verified, multiplexer_1_out, Enable);

  assign Offset = Instruction[15:5];
endmodule
