// Logisim project Ctl_Data_Processing.circ as structural Verilog: 1 circuit, main circuit Data_Processing
module Data_Processing (
  input  Enable,
  input  [15:0] Instruction,
  output [2:0] Rd,
  output [2:0] Rn,
  output [2:0] Rm,
  output [3:0] ALU_Opcode,
  output [3:0] Flags_Update_Mask
);

  wire comparator_1_eq, comparator_2_eq, comparator_3_eq, comparator_4_eq, comparator_6_eq, comparator_7_eq,
       comparator_8_eq, comparator_9_eq, comparator_10_eq, comparator_11_eq, comparator_12_eq,
       comparator_13_eq, comparator_14_eq, comparator_15_eq, comparator_16_eq, Update_All_flags, Update_NZ,
       Update_NZC;
  wire [3:0] and_2_out, and_3_out, and_4_out, bit_extender_2_out, bit_extender_3_out, bit_extender_4_out,
       bit_extender_5_out, or_3_out;
  wire [15:0] bit_extender_1_out;
  wire [15:10] and_1_out;

  assign bit_extender_1_out = {{15{Enable}}, Enable};  // Bit_Extender bit_extender_1
  assign {and_1_out, ALU_Opcode, Rm, Rd} = bit_extender_1_out & Instruction;  // AND_Gate and_1, 16 bits wide
  Comparator #(.width(4)) comparator_1 (.a(ALU_Opcode), .b(4'b0110), .eq(comparator_1_eq));  // open: gt, lt
  Comparator #(.width(4)) comparator_2 (.a(ALU_Opcode), .b(4'b1000), .eq(comparator_2_eq));  // open: gt, lt
  Comparator #(.width(4)) comparator_3 (.a(ALU_Opcode), .b(4'b1010), .eq(comparator_3_eq));  // open: gt, lt
  Comparator #(.width(4)) comparator_4 (.a(ALU_Opcode), .b(4'b1011), .eq(comparator_4_eq));  // open: gt, lt
  Comparator #(.width(4)) comparator_5 (.a(ALU_Opcode), .b(4'b1101), .eq(Update_NZ));  // open: gt, lt
  Comparator #(.width(4)) comparator_6 (.a(ALU_Opcode), .b(4'b0010), .eq(comparator_6_eq));  // open: gt, lt
  Comparator #(.width(4)) comparator_7 (.a(ALU_Opcode), .b(4'b0100), .eq(comparator_7_eq));  // open: gt, lt
  Comparator #(.width(4)) comparator_8 (.a(ALU_Opcode), .b(4'b0111), .eq(comparator_8_eq));  // open: gt, lt
  Comparator #(.width(4)) comparator_9 (.a(ALU_Opcode), .b(4'b1001), .eq(comparator_9_eq));  // open: gt, lt
  Comparator #(.width(4)) comparator_10 (.a(ALU_Opcode), .b(4'b1110), .eq(comparator_10_eq));  // open: gt, lt
  assign bit_extender_2_out = {{3{Update_All_flags}}, Update_All_flags};  // Bit_Extender bit_extender_2
  Comparator #(.width(4)) comparator_11 (.a(ALU_Opcode), .b(4'b0000), .eq(comparator_11_eq));  // open: gt, lt
  Comparator #(.width(4)) comparator_12 (.a(ALU_Opcode), .b(4'b0011), .eq(comparator_12_eq));  // open: gt, lt
  Comparator #(.width(4)) comparator_13 (.a(ALU_Opcode), .b(4'b0101), .eq(comparator_13_eq));  // open: gt, lt
  Comparator #(.width(4)) comparator_14 (.a(ALU_Opcode), .b(4'b1111), .eq(comparator_14_eq));  // open: gt, lt
  or or_1 (Update_All_flags, comparator_13_eq, comparator_1_eq, comparator_9_eq, comparator_3_eq, comparator_4_eq);
  Comparator #(.width(4)) comparator_15 (.a(ALU_Opcode), .b(4'b1100), .eq(comparator_15_eq));  // open: gt, lt
  assign bit_extender_3_out = {{3{Update_NZC}}, Update_NZC};  // Bit_Extender bit_extender_3
  Comparator #(.width(4)) comparator_16 (.a(ALU_Opcode), .b(4'b0001), .eq(comparator_16_eq));  // open: gt, lt
  assign bit_extender_4_out = {{3{Update_NZ}}, Update_NZ};  // Bit_Extender bit_extender_4
  or or_2 (Update_NZC, comparator_16_eq, comparator_6_eq, comparator_12_eq, comparator_7_eq, comparator_15_eq, comparator_10_eq, comparator_14_eq, comparator_8_eq, comparator_2_eq, comparator_11_eq);
  assign and_2_out = bit_extender_2_out & 4'b1111;  // AND_Gate and_2, 4 bits wide
  assign and_3_out = bit_extender_3_out & 4'b1110;  // AND_Gate and_3, 4 bits wide
  assign and_4_out = bit_extender_4_out & 4'b1100;  // AND_Gate and_4, 4 bits wide
  assign bit_extender_5_out = {{3{Enable}}, Enable};  // Bit_Extender bit_extender_5
  assign or_3_out = and_2_out | and_3_out | and_4_out;  // OR_Gate or_3, 4 bits wide
  assign Flags_Update_Mask = or_3_out & bit_extender_5_out;  // AND_Gate and_5, 4 bits wide

  assign Rn = Rd;

  // Other names for the same wires on the sheet: En = Enable
endmodule
