// Logisim project Ctl_Flags_APSR.circ as structural Verilog: 1 circuit, main circuit Flags_APSR
module Flags_APSR (
  input  [3:0] Update_Mask,
  input  [3:0] Flags_In,
  input  Clk,
  input  in_4,
  input  Rst,
  output [3:0] Flags_Out
);

  wire not_1_out;
  wire [3:0] multiplexer_1_out;

  not not_1 (not_1_out, in_4);
  Multiplexer multiplexer_1 (.in0(Flags_Out[0]), .in1(Flags_In[1]), .out(multiplexer_1_out[0]), .sel(Update_Mask[0]));
  Register #(.width(4)) register_1 (.D(multiplexer_1_out), .en(not_1_out), .clk(Clk), .Q(Flags_Out), .clr(Rst));
  Multiplexer multiplexer_2 (.in0(Flags_Out[1]), .in1(Flags_In[3]), .out(multiplexer_1_out[1]), .sel(Update_Mask[1]));
  Multiplexer multiplexer_3 (.in0(Flags_Out[2]), .in1(Flags_In[2]), .out(multiplexer_1_out[2]), .sel(Update_Mask[2]));
  Multiplexer multiplexer_4 (.in0(Flags_Out[3]), .in1(Flags_In[0]), .out(multiplexer_1_out[3]), .sel(Update_Mask[3]));
endmodule
