// Logisim project Ctl_Opcode_Decoder.circ as structural Verilog: 1 circuit, main circuit Opcode_Decoder
module Opcode_Decoder (
  input  [5:0] Opcode,
  output Shift,
  output Data_Processing,
  output Load_Store,
  output SP_Address,
  output Conditional
);

  wire and_2_out, and_3_out;

  and and_1 (Load_Store, Opcode[2], ~Opcode[3], ~Opcode[4], Opcode[5]);  // AND_Gate
  and and_2 (and_2_out, Opcode[2], ~Opcode[3], Opcode[4], Opcode[5]);  // AND_Gate
  and and_3 (and_3_out, ~Opcode[1], ~Opcode[2], Opcode[3], Opcode[4], Opcode[5]);  // AND_Gate
  nand nand_1 (Shift, Opcode[4], Opcode[5]);
  and and_4 (Data_Processing, ~Opcode[0], ~Opcode[1], ~Opcode[2], ~Opcode[3], Opcode[4], ~Opcode[5]);  // AND_Gate
  and and_5 (SP_Address, ~Opcode[0], ~Opcode[1], Opcode[2], Opcode[3], ~Opcode[4], Opcode[5]);  // AND_Gate
  or or_1 (Conditional, and_2_out, and_3_out);

  // Notes on the sheet:
  //   Shift, add, sub, mov
  //   SP Address
  //   Data Processing
  //   Load/Store
  //   Conditional branch
endmodule
